// Digital circuit A.dig as structural Verilog
module A (
  input  CLK,
  input  Ea,
  input  La,
  input  [7:0] DBs,
  output [7:0] Bs,
  output [7:0] QL
);

  assign Bs = Ea ? QL : 8'bz;  // Driver driver_1
  D_wEnable d_wenable_1 (
    .D0(DBs[0]), .D1(DBs[1]), .D2(DBs[2]), .D3(DBs[3]), .nE(La), .D4(DBs[4]), .D5(DBs[5]), .D6(DBs[6]),
    .D7(DBs[7]), .CLK(CLK), .Q0(QL[0]), .Q1(QL[1]), .Q2(QL[2]), .Q3(QL[3]), .Q4(QL[4]), .Q5(QL[5]),
    .Q6(QL[6]), .Q7(QL[7]));
endmodule
