// Digital circuit Accumulator.dig as structural Verilog
module Accumulator (
  input  [7:0] B,
  input  La,
  input  CLK,
  input  Ea,
  output [7:0] D,
  output [7:0] ASout
);

  assign D = Ea ? ASout : 8'bz;  // Driver driver_1
  D8_wEnableAsyncClear d8_wenableasyncclear_1 (
    .D0(B[0]), .D1(B[1]), .D2(B[2]), .D3(B[3]), .D4(B[4]), .D5(B[5]), .D6(B[6]), .D7(B[7]), .nE(La),
    .CLK(CLK), .CLR(1'b0), .Q0(ASout[0]), .Q1(ASout[1]), .Q2(ASout[2]), .Q3(ASout[3]), .Q4(ASout[4]),
    .Q5(ASout[5]), .Q6(ASout[6]), .Q7(ASout[7]));

  // Notes on the sheet:
  //   B: Input coming from the bus
  //   D: Output going to the bus
endmodule
