// Digital circuit Adder-Subtractor.dig as structural Verilog
module Adder_Subtractor (
  input  [7:0] Bin,
  input  Su,
  input  [7:0] Ain,
  input  Eu,
  output [7:0] D
);

  wire [7:0] add_1_s, multiplexer_1_out, sub_1_s;

  assign D = Eu ? multiplexer_1_out : 8'bz;  // Driver driver_1
  Multiplexer #(.Bits(8)) multiplexer_1 (.sel(Su), .in_0(add_1_s), .in_1(sub_1_s), .out(multiplexer_1_out));
  Sub #(.Bits(8)) sub_1 (.a(Ain), .b(Bin), .c_i(1'b0), .s(sub_1_s));  // open: c_o
  Add #(.Bits(8)) add_1 (.a(Ain), .b(Bin), .c_i(1'b0), .s(add_1_s));  // open: c_o

  // Notes on the sheet:
  //   Bin: Input coming from the accumulator
  //   D: Output going to the bus
  //   Su: Selector
  //   Ain: Input coming from the accumulator
  //   Eu: Selector
endmodule
