// Digital circuit IR.dig as structural Verilog
module IR (
  input  [7:0] B,
  input  nLi,
  input  nEi,
  input  CLK,
  input  CLR,
  output [3:0] C,
  output [3:0] D
);

  wire not_1_out;
  wire [3:0] d8_wenableasyncclear_1_q3;

  not not_1 (not_1_out, nEi);
  D8_wEnableAsyncClear d8_wenableasyncclear_1 (
    .D0(B[0]), .D1(B[1]), .D2(B[2]), .D3(B[3]), .D4(B[4]), .D5(B[5]), .D6(B[6]), .D7(B[7]), .nE(nLi),
    .CLK(CLK), .CLR(CLR), .Q0(d8_wenableasyncclear_1_q3[0]), .Q1(d8_wenableasyncclear_1_q3[1]),
    .Q2(d8_wenableasyncclear_1_q3[2]), .Q3(d8_wenableasyncclear_1_q3[3]), .Q4(C[0]), .Q5(C[1]), .Q6(C[2]),
    .Q7(C[3]));
  assign D = not_1_out ? d8_wenableasyncclear_1_q3 : 4'bz;  // Driver driver_1

  // Notes on the sheet:
  //   B: Input coming from bus
  //   C: Output going to the controller
  //   D: Output going to the bus
endmodule
