// Digital circuit Input and MAR.dig as structural Verilog
module Input_and_MAR (
  input  [3:0] B,
  input  Lm,
  input  CLK,
  output [3:0] Q
);

  // D4_wEnableAsyncClear d4_wenableasyncclear_1: pin names not known; wires that end beside it: Q[3], Q[2], Q[1], Q[0], 1'b0, CLK, Lm, B[3], B[2], B[1], B[0]

  // Notes on the sheet:
  //   B: Input coming from the bus
  //   Q: Output going to the controller
endmodule
