// Digital circuit MAR.dig as structural Verilog
module MAR (
  input  CLK,
  input  La,
  input  [3:0] DBs,
  output [3:0] Q
);

  // D4_wEnable d4_wenable_1: pin names not known; wires that end beside it: Q[3], Q[2], Q[1], Q[0], CLK, La, DBs[3], DBs[2], DBs[1], DBs[0]
endmodule
