// Digital circuit Output Register.dig as structural Verilog
module Output_Register (
  input  [7:0] B,
  input  Lo,
  input  CLK,
  output [7:0] Q
);

  D8_wEnableAsyncClear d8_wenableasyncclear_1 (
    .D0(B[0]), .D1(B[1]), .D2(B[2]), .D3(B[3]), .D4(B[4]), .D5(B[5]), .D6(B[6]), .D7(B[7]), .nE(Lo),
    .CLK(CLK), .CLR(1'b0), .Q0(Q[0]), .Q1(Q[1]), .Q2(Q[2]), .Q3(Q[3]), .Q4(Q[4]), .Q5(Q[5]), .Q6(Q[6]),
    .Q7(Q[7]));

  // Notes on the sheet:
  //   B: Input coming from the bus
  //   Q: Output going to adder-subtractor
endmodule
