// Digital circuit Program Counter.dig as structural Verilog
module Program_Counter (
  input  Cp,
  input  CLK,
  input  CLR,
  input  Ep,
  output [3:0] D
);

  wire not_1_out;
  wire [3:0] counter_1_out;

  not not_1 (not_1_out, CLR);
  Counter #(.Bits(4)) counter_1 (.en(Cp), .C(CLK), .clr(not_1_out), .out(counter_1_out));  // open: ovf
  assign D = Ep ? counter_1_out : 4'bz;  // Driver driver_1

  // Notes on the sheet:
  //   D: Output going to the bus
endmodule
