// Digital circuit SA1-P Architecture.dig as structural Verilog
module SA1_P_Architecture (
  input  Main_Clock,
  input  Self_Start_Switch
);

  wire CLK, CLR, Cp, Ea, Ep, Eu, HLT, nCE, nCLK, nCLR, nEi, nLa, nLb, nLi, nLm, nLo, not_3_out, RESET_out,
       Su, T1, T3;
  wire [3:0] input_and_mar_1_q, ir_1_c, output_register_1_q, output_register_1_q_2, program_counter_1_d;
  wire [7:0] accumulator_1_asout, b_register_1_q, rom_1_d;

  Button RESET (.out(RESET_out));
  RS_FF_AS rs_ff_as_1 (.S(Self_Start_Switch), .R(RESET_out), .nQ(CLR));  // open: Q
  and and_1 (CLK, Main_Clock, HLT);
  TCounter tcounter_1 (.CLK(CLK), .CLR(CLR), .T1(T1), .T4(T3));  // open: T2, T3, T5, T6
  not not_1 (nCLR, CLR);
  not not_2 (nCLK, CLK);
  nand nand_1 (HLT, ir_1_c[3], ir_1_c[2], ir_1_c[1], ir_1_c[0]);
  not not_3 (not_3_out, nCE);
  Program_Counter program_counter_1 (.Ep(Ep), .Cp(Cp), .CLK(nCLK), .CLR(nCLR), .D(program_counter_1_d));
  Input_and_MAR input_and_mar_1 (.B(program_counter_1_d), .Q(input_and_mar_1_q), .Lm(nLm), .CLK(CLK));
  ROM #(.AddrBits(4), .Bits(8)) rom_1 (.A(input_and_mar_1_q), .sel(not_3_out), .D(rom_1_d));
  IR ir_1 (.B(rom_1_d), .D(program_counter_1_d), .C(ir_1_c), .nEi(nEi), .nLi(nLi), .CLK(CLK), .CLR(CLR));
  // Probe on ir_1_c
  Sequencer sequencer_1 (
    .CLK(nCLK), .T3(T3), .T1(T1), .CLR(CLR), .I(ir_1_c),
    .CON({Cp, Ep, nLm, nCE, nLi, nEi, nLa, Ea, Su, Eu, nLb, nLo}));
  // Probe on input_and_mar_1_q
  // Probe on {Cp, Ep, nLm, nCE, nLi, nEi, nLa, Ea, Su, Eu, nLb, nLo}
  Accumulator accumulator_1 (.B(rom_1_d), .D(rom_1_d), .CLK(CLK), .La(nLa), .Ea(Ea), .ASout(accumulator_1_asout));
  Adder_Subtractor adder_subtractor_1 (.Bin(b_register_1_q), .D(rom_1_d), .Su(Su), .Eu(Eu), .Ain(accumulator_1_asout));
  B_register b_register_1 (.CLK(CLK), .Lb(nLb), .B(rom_1_d), .Q(b_register_1_q));
  Output_Register output_register_1 (
    .B(rom_1_d), .CLK(CLK), .Lo(nLo), .Q({output_register_1_q_2, output_register_1_q}));
  // Probe on accumulator_1_asout
  // Probe on b_register_1_q
  Seven_Seg_Hex seven_seg_hex_1 (.d(output_register_1_q_2), .dp(1'b0));
  Seven_Seg_Hex seven_seg_hex_2 (.d(output_register_1_q), .dp(1'b0));

  // Notes on the sheet:
  //   Main_Clock: Hz: 5
  //   #HLT: maka affect sya sa pag display. Dapat sa pinaka last lang mag hlt kay
  //   if mag hlt unya naapay laing iprocess, dili nato niya ma display ug tarong
  //   16X8
  //   contents of rom_1 (hex, n*v repeats v):
  //   f,e0,e,e0,2f,e0,0,0,0,0,0,0,0,0,2,5
endmodule
