// Digital circuit Sequencer.dig as structural Verilog
module Sequencer (
  input  CLK,
  input  T3,
  input  T1,
  input  CLR,
  input  [3:0] I,
  output [11:0] CON
);

  wire not_1_out, not_2_out, or_1_out;
  wire [3:0] AddressROM_d, counter4wasyncclear_1_qa;

  not not_1 (not_1_out, T3);
  or or_1 (or_1_out, T1, CLR);
  ROM #(.AddrBits(4), .Bits(4)) AddressROM (.A(I), .sel(1'b1), .D(AddressROM_d));
  // Probe on AddressROM_d
  not not_2 (not_2_out, or_1_out);
  Counter4wAsyncClear counter4wasyncclear_1 (
    .nLD(not_1_out), .nCLR(not_2_out), .CLK(CLK), .ENT(1'b1), .ENP(1'b1), .A(AddressROM_d[0]),
    .B(AddressROM_d[1]), .C(AddressROM_d[2]), .D(AddressROM_d[3]), .QA(counter4wasyncclear_1_qa[0]),
    .QB(counter4wasyncclear_1_qa[1]), .QC(counter4wasyncclear_1_qa[2]), .QD(counter4wasyncclear_1_qa[3]));  // open: RCO
  ROM #(.AddrBits(4), .Bits(12)) ControlROM (.A(counter4wasyncclear_1_qa), .sel(1'b1), .D(CON));

  // Notes on the sheet:
  //   contents of AddressROM (hex, n*v repeats v):
  //   3,6,9,0,0,0,0,0,0,0,0,0,0,0,c
  //   contents of ControlROM (hex, n*v repeats v):
  //   5ba,d3e,11e,43a,12e,53e,43a,136,56e,43a,136,56f,72d,53e,53e
endmodule
